# Fritzing sketch thermostat-bb2 (saved by Fritzing 0.9.3b)
circuit board: 6.48945cm x 4.95311cm
perfboards: 1

parts:
  Contactor = Screw terminal - 2 pins [package=THT]
  R1 = Resistor [tolerance=±5% resistance=4.7k package=THT]
  DIP-Relay1 = DIP-Relay-D31A [part_number=D31A*]
  DISPLAY = shrouded pin header, 16 pins [form="♂ (shrouded male)"]
  SENS = Screw terminal - 2 pins [package=THT]
  R3 = Resistor [tolerance=±5% resistance=1k package=THT]
  R4 = Resistor [tolerance=±5% resistance=1k package=THT]
  R5 = Resistor [tolerance=±5% resistance=1k package=THT]
  BTN = Screw terminal - 2 pins [package=THT]
  BTN-PWR = Screw terminal - 2 pins [package=THT]
  Arduino_Nano_3 = Arduino Nano (Rev3.0)

nets:
  N1: Contactor.pin1, DIP-Relay1.B2_Switch_Terminal_B
  N2: Contactor.pin2, DIP-Relay1.A2_Switch_Terminal_A
  N3: R1.Pin_0, SENS.pin2, Arduino_Nano_3.D7
  N4: R1.Pin_1, DISPLAY.pin16, R5.Pin_0, BTN-PWR.pin2, Arduino_Nano_3.5V
  N5: DIP-Relay1.COIL1_+, Arduino_Nano_3.D8
  N6: DIP-Relay1.Coil2_-, DISPLAY.pin1, DISPLAY.pin3, DISPLAY.pin9, SENS.pin1, R3.Pin_1, BTN-PWR.pin1, Arduino_Nano_3.GND
  N7: DISPLAY.pin2, R4.Pin_1
  N8: DISPLAY.pin6, Arduino_Nano_3.D5
  N9: DISPLAY.pin7, Arduino_Nano_3.D3
  N10: DISPLAY.pin8, R5.Pin_1
  N11: DISPLAY.pin10, Arduino_Nano_3.D2
  N12: DISPLAY.pin11, Arduino_Nano_3.D4
  N13: DISPLAY.pin14, Arduino_Nano_3.D11/MOSI
  N14: DISPLAY.pin15, Arduino_Nano_3.D12/MISO
  N15: R3.Pin_0, R4.Pin_0
  N16: BTN.pin1, Arduino_Nano_3.A1
  N17: BTN.pin2, Arduino_Nano_3.A2
